# Fritzing sketch WiringDiagram (saved by Fritzing 0.9.5d)

parts:
  NodeMCU_Board = NodeMCU V3.0
  RFID = RFID-RC522 [part_number=101218]
  Alarm_Status_Connector = Keyes Relay [package=THT]
  Contact_siren = Keyes Relay [package=THT]
  Door_Contact = Magnetic Door Switch [package=reed_switch_plastic]
  Tamper = D2F-FL Omron Snap Action Limit Switch with Level

nets:
  N1: NodeMCU_Board.D1, Door_Contact.1
  N2: NodeMCU_Board.D2, Contact_siren.signal
  N3: NodeMCU_Board.D3, RFID.RST
  N4: NodeMCU_Board.D4, RFID.SDA
  3V3: NodeMCU_Board.3V3, RFID.3.3V, Tamper.COM
  GND: NodeMCU_Board.GND, RFID.GND, Alarm_Status_Connector.ground, Contact_siren.ground, Door_Contact.2
  N5: NodeMCU_Board.D5, RFID.SCK
  N6: NodeMCU_Board.D6, RFID.MISO
  N7: NodeMCU_Board.D7, RFID.MOSI
  N8: NodeMCU_Board.D8, Alarm_Status_Connector.signal
  N9: NodeMCU_Board.Vin, Alarm_Status_Connector.power, Contact_siren.power
  N10: NodeMCU_Board.A0, Tamper.NO

notes:
  Wiring diagram created by Alessandro Annese.
  Last update: 31/03/2020
  github.com/Ax3lFernus/NodeMCU_WiFi_Alarm/

custom parts:
  NodeMCU V3.0: ESP8266 based NodeMCU
  Keyes Relay: The Keyes 5V relay module is suitable for SCM development, home appliance control. It uses a 5V~12V TIL control signal which can control DC / AC signal.
  D2F-FL Omron Snap Action Limit Switch with Level: Snap action switch with stainless steel lever.
